// Logisim project criptoULA.circ as structural Verilog: 5 circuits, main circuit main
module main (
  input  [6:0] Chave,
  input  _0___XOR__1___Cesar,
  input  _0___cript___1___decript,
  input  Enable
);

  wire and_1_out, clock_1_out, keyboard_1_avail, Reset_out;
  wire [6:0] keyboard_1_data, ula_1_output;

  Button Reset (.out(Reset_out));
  Clock clock_1 (.out(clock_1_out));
  Keyboard keyboard_1 (
    .clk(clock_1_out), .re(Enable), .clr(Reset_out), .avail(keyboard_1_avail), .data(keyboard_1_data));
  ULA ula_1 (
    .A__caractere(keyboard_1_data), .B__chave(Chave),
    .Operacao({_0___XOR__1___Cesar, _0___cript___1___decript}), .Output(ula_1_output));
  and and_1 (and_1_out, keyboard_1_avail, Enable);
  TTY tty_1 (.data(keyboard_1_data), .clk(clock_1_out), .we(and_1_out), .clr(Reset_out));
  TTY tty_2 (.data(ula_1_output), .clk(clock_1_out), .we(and_1_out), .clr(Reset_out));

  // Notes on the sheet:
  //   Digite o texto
  //   INPUT
  //   OUTPUT
endmodule

module ULA (
  input  [6:0] A__caractere,
  input  [6:0] B__chave,
  input  [1:0] Operacao,
  output [6:0] Output
);

  wire [6:0] A_Caesar, A_deCaesar, A_XOR, B_Caesar, B_deCaesar, B_XOR, caesar_coder_1_output,
       caesar_decoder_1_output, demultiplexer_1_out0, demultiplexer_1_out1, demultiplexer_2_out0,
       demultiplexer_2_out1, xor_1_out;

  Demultiplexer #(.select(2), .width(7), .enable("false")) demultiplexer_1 (
    .out0(demultiplexer_1_out0), .out1(demultiplexer_1_out1), .out2(A_Caesar), .out3(A_deCaesar),
    .in(A__caractere), .sel(Operacao));
  Demultiplexer #(.select(2), .width(7), .enable("false")) demultiplexer_2 (
    .out0(demultiplexer_2_out0), .out1(demultiplexer_2_out1), .out2(B_Caesar), .out3(B_deCaesar),
    .in(B__chave), .sel(Operacao));
  assign A_XOR = demultiplexer_1_out0 | demultiplexer_1_out1;  // OR_Gate or_1, 7 bits wide
  assign B_XOR = demultiplexer_2_out0 | demultiplexer_2_out1;  // OR_Gate or_2, 7 bits wide
  assign xor_1_out = A_XOR ^ B_XOR;  // XOR_Gate xor_1, 7 bits wide
  Caesar_coder caesar_coder_1 (
    .Caractere_ASCII_de_7_bits(A_Caesar), .Deslocamento(B_Caesar), .Output(caesar_coder_1_output));
  Caesar_decoder caesar_decoder_1 (
    .Caractere_ASCII_de_7_bits(A_deCaesar), .Deslocamento(B_deCaesar), .Output(caesar_decoder_1_output));
  Multiplexer #(.select(2), .width(7), .enable("false")) multiplexer_1 (
    .in0(xor_1_out), .in1(xor_1_out), .in2(caesar_coder_1_output), .in3(caesar_decoder_1_output),
    .out(Output), .sel(Operacao));
endmodule

module Caesar_coder (
  input  [6:0] Caractere_ASCII_de_7_bits,
  input  [6:0] Deslocamento,
  output [6:0] Output
);

  wire \alphabet_tester_1_é_letra , \alphabet_tester_1_é_letra_minúscula , \alphabet_tester_2_é_letra ,
       \alphabet_tester_2_é_letra_minúscula , and_1_out, xnor_1_out;
  wire [6:0] adder_1_out, divider_1_rem, multiplexer_1_out, subtractor_1_out;

  Divider #(.width(7)) divider_1 (.a(Deslocamento), .b(7'b0011010), .rem(divider_1_rem));  // open: out, upper
  Adder #(.width(7)) adder_1 (.a(Caractere_ASCII_de_7_bits), .b(divider_1_rem), .out(adder_1_out));  // open: cin, cout
  Subtractor #(.width(7)) subtractor_1 (.a(adder_1_out), .b(7'b0011010), .out(subtractor_1_out));  // open: bin, bout
  Alphabet_tester alphabet_tester_1 (
    .Caractere_ASCII_de_7_bits(adder_1_out), .\É_letra (\alphabet_tester_1_é_letra ),
    .\É_letra_minúscula (\alphabet_tester_1_é_letra_minúscula ));  // open: É_letra_maiúscula
  Multiplexer #(.width(7), .enable("false")) multiplexer_1 (
    .in0(subtractor_1_out), .in1(adder_1_out), .out(multiplexer_1_out), .sel(and_1_out));
  and and_1 (and_1_out, \alphabet_tester_1_é_letra , xnor_1_out);
  xnor xnor_1 (xnor_1_out, \alphabet_tester_1_é_letra_minúscula , \alphabet_tester_2_é_letra_minúscula );
  Multiplexer #(.width(7), .enable("false")) multiplexer_2 (
    .in0(Caractere_ASCII_de_7_bits), .in1(multiplexer_1_out), .out(Output), .sel(\alphabet_tester_2_é_letra ));
  Alphabet_tester alphabet_tester_2 (
    .Caractere_ASCII_de_7_bits(Caractere_ASCII_de_7_bits), .\É_letra (\alphabet_tester_2_é_letra ),
    .\É_letra_minúscula (\alphabet_tester_2_é_letra_minúscula ));  // open: É_letra_maiúscula
endmodule

module Alphabet_tester (
  input  [6:0] Caractere_ASCII_de_7_bits,
  output \É_letra_maiúscula ,
  output \É_letra ,
  output \É_letra_minúscula 
);

  wire comparator_1_gt, comparator_2_lt, comparator_3_gt, comparator_4_lt;

  Comparator #(.width(7), .mode("unsigned")) comparator_1 (
    .a(Caractere_ASCII_de_7_bits), .b(7'b1000000), .gt(comparator_1_gt));  // open: eq, lt
  Comparator #(.width(7), .mode("unsigned")) comparator_2 (
    .a(Caractere_ASCII_de_7_bits), .b(7'b1011011), .lt(comparator_2_lt));  // open: gt, eq
  Comparator #(.width(7), .mode("unsigned")) comparator_3 (
    .a(Caractere_ASCII_de_7_bits), .b(7'b1100000), .gt(comparator_3_gt));  // open: eq, lt
  Comparator #(.width(7), .mode("unsigned")) comparator_4 (
    .a(Caractere_ASCII_de_7_bits), .b(7'b1111011), .lt(comparator_4_lt));  // open: gt, eq
  and and_1 (\É_letra_maiúscula , comparator_1_gt, comparator_2_lt);
  and and_2 (\É_letra_minúscula , comparator_3_gt, comparator_4_lt);
  or or_1 (\É_letra , \É_letra_maiúscula , \É_letra_minúscula );
endmodule

module Caesar_decoder (
  input  [6:0] Caractere_ASCII_de_7_bits,
  input  [6:0] Deslocamento,
  output [6:0] Output
);

  wire \alphabet_tester_1_é_letra , \alphabet_tester_1_é_letra_minúscula , \alphabet_tester_2_é_letra ,
       \alphabet_tester_2_é_letra_minúscula , and_1_out, xnor_1_out;
  wire [6:0] adder_1_out, divider_1_rem, multiplexer_1_out, subtractor_1_out;

  Divider #(.width(7)) divider_1 (.a(Deslocamento), .b(7'b0011010), .rem(divider_1_rem));  // open: out, upper
  Subtractor #(.width(7)) subtractor_1 (
    .a(Caractere_ASCII_de_7_bits), .b(divider_1_rem), .out(subtractor_1_out));  // open: bin, bout
  Adder #(.width(7)) adder_1 (.a(subtractor_1_out), .b(7'b0011010), .out(adder_1_out));  // open: cin, cout
  Alphabet_tester alphabet_tester_1 (
    .Caractere_ASCII_de_7_bits(subtractor_1_out), .\É_letra (\alphabet_tester_1_é_letra ),
    .\É_letra_minúscula (\alphabet_tester_1_é_letra_minúscula ));  // open: É_letra_maiúscula
  Multiplexer #(.width(7), .enable("false")) multiplexer_1 (
    .in0(adder_1_out), .in1(subtractor_1_out), .out(multiplexer_1_out), .sel(and_1_out));
  and and_1 (and_1_out, \alphabet_tester_1_é_letra , xnor_1_out);
  xnor xnor_1 (xnor_1_out, \alphabet_tester_1_é_letra_minúscula , \alphabet_tester_2_é_letra_minúscula );
  Multiplexer #(.width(7), .enable("false")) multiplexer_2 (
    .in0(Caractere_ASCII_de_7_bits), .in1(multiplexer_1_out), .out(Output), .sel(\alphabet_tester_2_é_letra ));
  Alphabet_tester alphabet_tester_2 (
    .Caractere_ASCII_de_7_bits(Caractere_ASCII_de_7_bits), .\É_letra (\alphabet_tester_2_é_letra ),
    .\É_letra_minúscula (\alphabet_tester_2_é_letra_minúscula ));  // open: É_letra_maiúscula
endmodule
